// Logisim project progetto.circ as structural Verilog: 8 circuits, main circuit main
module main (
  output [4:0] out_1,
  output [4:0] out_2,
  output [4:0] out_3,
  output [4:0] out_4
);

  wire _0_out, _1_out, _2_out, _3_out, _4_out, _5_out, _6_out, _7_out, _8_out, _9_out, button_2_out,
       button_out, CLK_out, keypad_1_clicked, meno, of, OK_out, or_1_out, Reset;
  wire [1:0] counter_1_q;
  wire [3:0] keypad_1_b0;
  wire [4:0] and_1_out, calcolo_1_out_5, multiplexer_1_out, negativator_1_out_2, X_q;
  wire [31:0] xy_selector_1_x0_output, xy_selector_1_x1_output, xy_selector_1_x2_output,
       xy_selector_1_x3_output, xy_selector_1_x4_output, xy_selector_1_x5_output, xy_selector_1_x6_output,
       xy_selector_1_x7_output, xy_selector_1_x8_output, xy_selector_1_x9_output, xy_selector_1_x10_output,
       xy_selector_1_x11_output, xy_selector_1_x12_output, xy_selector_1_x13_output,
       xy_selector_1_x14_output, xy_selector_1_x15_output, xy_selector_1_x16_output,
       xy_selector_1_x17_output, xy_selector_1_x18_output, xy_selector_1_x19_output,
       xy_selector_1_x20_output, xy_selector_1_x21_output, xy_selector_1_x22_output,
       xy_selector_1_x23_output, xy_selector_1_x24_output, xy_selector_1_x25_output,
       xy_selector_1_x26_output, xy_selector_1_x27_output, xy_selector_1_x28_output,
       xy_selector_1_x29_output, xy_selector_1_x30_output, xy_selector_1_x31_output;

  Button R (.out(Reset));
  Button _8 (.out(_8_out));
  Button _7 (.out(_7_out));
  Button _4 (.out(_4_out));
  Button _5 (.out(_5_out));
  Button _1 (.out(_1_out));
  Button _2 (.out(_2_out));
  Button _0 (.out(_0_out));
  Button OK (.out(OK_out));
  Button button (.out(button_out));
  DotMatrix #(.matrixcols(32), .matrixrows(32)) dotmatrix_1 (
    .col0(xy_selector_1_x0_output), .col1(xy_selector_1_x1_output), .col2(xy_selector_1_x2_output),
    .col3(xy_selector_1_x3_output), .col4(xy_selector_1_x4_output), .col5(xy_selector_1_x5_output),
    .col6(xy_selector_1_x6_output), .col7(xy_selector_1_x7_output), .col8(xy_selector_1_x8_output),
    .col9(xy_selector_1_x9_output), .col10(xy_selector_1_x10_output), .col11(xy_selector_1_x11_output),
    .col12(xy_selector_1_x12_output), .col13(xy_selector_1_x13_output), .col14(xy_selector_1_x14_output),
    .col15(xy_selector_1_x15_output), .col16(xy_selector_1_x16_output), .col17(xy_selector_1_x17_output),
    .col18(xy_selector_1_x18_output), .col19(xy_selector_1_x19_output), .col20(xy_selector_1_x20_output),
    .col21(xy_selector_1_x21_output), .col22(xy_selector_1_x22_output), .col23(xy_selector_1_x23_output),
    .col24(xy_selector_1_x24_output), .col25(xy_selector_1_x25_output), .col26(xy_selector_1_x26_output),
    .col27(xy_selector_1_x27_output), .col28(xy_selector_1_x28_output), .col29(xy_selector_1_x29_output),
    .col30(xy_selector_1_x30_output), .col31(xy_selector_1_x31_output));
  xy_selector xy_selector_1 (
    .x(X_q), .y(and_1_out), .x16_output(xy_selector_1_x16_output), .CLK(CLK_out),
    .x17_output(xy_selector_1_x17_output), .x18_output(xy_selector_1_x18_output),
    .x19_output(xy_selector_1_x19_output), .x20_output(xy_selector_1_x20_output),
    .x21_output(xy_selector_1_x21_output), .x22_output(xy_selector_1_x22_output),
    .x23_output(xy_selector_1_x23_output), .x24_output(xy_selector_1_x24_output),
    .x25_output(xy_selector_1_x25_output), .x26_output(xy_selector_1_x26_output),
    .x27_output(xy_selector_1_x27_output), .x28_output(xy_selector_1_x28_output),
    .x29_output(xy_selector_1_x29_output), .x30_output(xy_selector_1_x30_output),
    .x31_output(xy_selector_1_x31_output), .x0_output(xy_selector_1_x0_output),
    .x1_output(xy_selector_1_x1_output), .x2_output(xy_selector_1_x2_output),
    .x3_output(xy_selector_1_x3_output), .x4_output(xy_selector_1_x4_output),
    .x5_output(xy_selector_1_x5_output), .x6_output(xy_selector_1_x6_output),
    .x7_output(xy_selector_1_x7_output), .x8_output(xy_selector_1_x8_output),
    .x9_output(xy_selector_1_x9_output), .x10_output(xy_selector_1_x10_output),
    .x11_output(xy_selector_1_x11_output), .x12_output(xy_selector_1_x12_output),
    .x13_output(xy_selector_1_x13_output), .x14_output(xy_selector_1_x14_output),
    .x15_output(xy_selector_1_x15_output), .of(of), .Reset(Reset));
  Button _9 (.out(_9_out));
  Button _6 (.out(_6_out));
  Button _3 (.out(_3_out));
  Button button_2 (.out(button_2_out));
  or or_1 (or_1_out, OK_out, button_out);
  keypad keypad_1 (
    ._0(_0_out), ._1(_1_out), ._3(_3_out), ._2(_2_out), ._5(_5_out), ._4(_4_out), ._7(_7_out), ._6(_6_out),
    .b2_2(keypad_1_b0[2]), .b1(keypad_1_b0[1]), .b0(keypad_1_b0[0]), ._8(_8_out), ._9(_9_out),
    .b2(keypad_1_b0[3]), .clicked(keypad_1_clicked));
  minus minus_1 (.in_1(button_2_out), .out_2(meno));
  Counter #(.width(2), .max('h2), .trigger("falling")) counter_1 (
    .Q(counter_1_q), .clk(or_1_out), .clr(Reset));  // open: load, D, count, carry
  LED u_meno (.in(meno));
  Multiplexer #(.width(5)) multiplexer_1 (
    .in0({1'b0, keypad_1_b0}), .in1(negativator_1_out_2), .out(multiplexer_1_out), .sel(meno));  // open: en
  negativator negativator_1 (.in_1({1'b0, keypad_1_b0}), .out_2(negativator_1_out_2));
  Counter #(.width(5), .max('h1f)) X (.Q(X_q), .clk(CLK_out), .clr(Reset));  // open: load, D, count, carry
  Clock CLK (.out(CLK_out));
  memory memory_1 (
    .in_1(multiplexer_1_out), .in_2(keypad_1_clicked), .in_3(OK_out), .in_4(counter_1_q), .out_6(out_1),
    .out_7(out_2), .out_8(out_3), .out_9(out_4), .Reset(Reset));
  calcolo calcolo_1 (.c_x_2(out_1), .c_x(out_2), .q(out_3), .out_5(calcolo_1_out_5), .x(X_q), .out_6(of));
  assign and_1_out = calcolo_1_out_5 & ~{5{of}};  // AND_Gate and_1, 5 bits wide
endmodule

module keypad (
  input  _0,
  input  _1,
  input  _3,
  input  _2,
  input  _5,
  input  _4,
  input  _7,
  input  _6,
  input  _9,
  input  _8,
  output clicked,
  output b2,
  output b2_2,
  output b1,
  output b0
);

  or or_1 (b0, _1, _9, _3, _5, _7);
  or or_2 (b1, _3, _2, _7, _6);
  or or_3 (b2_2, _6, _5, _7, _4);
  or or_4 (b2, _9, _8);
  or or_5 (clicked, _0, b0, b1, b2_2, b2);
endmodule

module negativator (
  input  [4:0] in_1,
  output [4:0] out_2
);

  wire [4:0] not_1_out;

  assign not_1_out = ~in_1;  // NOT_Gate not_1, 5 bits wide
  Adder #(.width(5)) adder_1 (.a(not_1_out), .b(5'b00001), .out(out_2));  // open: cin, cout
endmodule

module memory (
  input  [4:0] in_1,
  input  in_2,
  input  in_3,
  input  [1:0] in_4,
  input  Reset,
  output [4:0] out_6,
  output [4:0] out_7,
  output [4:0] out_8,
  output [4:0] out_9
);

  wire demultiplexer_2_out0, demultiplexer_2_out1, demultiplexer_2_out2, demultiplexer_2_out3;
  wire [4:0] d_ff_1_q, demultiplexer_1_out0, demultiplexer_1_out1, demultiplexer_1_out2, demultiplexer_1_out3;

  D_Flip_Flop #(.trigger("high")) d_ff_1 (.clk(in_2), .D(in_1[0]), .Q(d_ff_1_q[0]));  // open: Qn, preset, en, reset
  D_Flip_Flop #(.trigger("high")) d_ff_2 (.clk(in_2), .D(in_1[1]), .Q(d_ff_1_q[1]));  // open: Qn, preset, en, reset
  D_Flip_Flop #(.trigger("high")) d_ff_3 (.clk(in_2), .D(in_1[2]), .Q(d_ff_1_q[2]));  // open: Qn, preset, en, reset
  D_Flip_Flop #(.trigger("high")) d_ff_4 (.clk(in_2), .D(in_1[3]), .Q(d_ff_1_q[3]));  // open: Qn, preset, en, reset
  D_Flip_Flop #(.trigger("high")) d_ff_5 (.clk(in_2), .D(in_1[4]), .Q(d_ff_1_q[4]));  // open: Qn, preset, en, reset
  Demultiplexer #(.select(2), .width(5)) demultiplexer_1 (
    .out0(demultiplexer_1_out0), .out1(demultiplexer_1_out1), .out2(demultiplexer_1_out2),
    .out3(demultiplexer_1_out3), .in(d_ff_1_q), .sel(in_4));  // open: en
  Demultiplexer #(.select(2)) demultiplexer_2 (
    .out0(demultiplexer_2_out0), .out1(demultiplexer_2_out1), .out2(demultiplexer_2_out2),
    .out3(demultiplexer_2_out3), .in(in_3), .sel(in_4));  // open: en
  Register #(.width(5), .trigger("high")) register_1 (
    .D(demultiplexer_1_out0), .Q(out_6), .clk(demultiplexer_2_out0), .clr(Reset));  // open: en
  Register #(.width(5), .trigger("high")) register_2 (
    .D(demultiplexer_1_out1), .Q(out_7), .clk(demultiplexer_2_out1), .clr(Reset));  // open: en
  Register #(.width(5), .trigger("high")) register_3 (
    .D(demultiplexer_1_out2), .Q(out_8), .clk(demultiplexer_2_out2), .clr(Reset));  // open: en
  Register #(.width(5), .trigger("high")) register_4 (
    .D(demultiplexer_1_out3), .Q(out_9), .clk(demultiplexer_2_out3), .clr(Reset));  // open: en
endmodule

module minus (
  input  in_1,
  output out_2
);

  wire and_1_out, d_ff_1_qn;

  and and_1 (and_1_out, in_1, d_ff_1_qn);
  D_Flip_Flop #(.trigger("falling")) d_ff_1 (
    .clk(in_1), .D(and_1_out), .Q(out_2), .Qn(d_ff_1_qn));  // open: preset, en, reset
endmodule

module calcolo (
  input  [4:0] c_x_2,
  input  [4:0] c_x,
  input  [4:0] q,
  input  [4:0] x,
  output [4:0] out_5,
  output out_6
);

  wire adder_1_cout, adder_2_cout;
  wire [4:0] adder_1_out, multiplier_1_cout, multiplier_1_out, multiplier_2_cout, multiplier_2_out,
       multiplier_3_cout, multiplier_3_out;

  Multiplier #(.width(5)) multiplier_1 (.a(c_x), .b(x), .out(multiplier_1_out), .cout(multiplier_1_cout));  // open: cin
  Multiplier #(.width(5)) multiplier_2 (
    .a(c_x_2), .b(x), .out(multiplier_2_out), .cout(multiplier_2_cout));  // open: cin
  Multiplier #(.width(5)) multiplier_3 (
    .a(multiplier_2_out), .b(x), .out(multiplier_3_out), .cout(multiplier_3_cout));  // open: cin
  Adder #(.width(5)) adder_1 (
    .a(multiplier_3_out), .b(multiplier_1_out), .out(adder_1_out), .cout(adder_1_cout));  // open: cin
  Adder #(.width(5)) adder_2 (.a(q), .b(adder_1_out), .out(out_5), .cin(adder_1_cout), .cout(adder_2_cout));
  or or_1 (out_6, adder_2_cout, multiplier_3_cout[0], multiplier_3_cout[1], multiplier_3_cout[2], multiplier_3_cout[3], multiplier_3_cout[4], multiplier_1_cout[0], multiplier_1_cout[1], multiplier_1_cout[2], multiplier_1_cout[3], multiplier_1_cout[4], multiplier_2_cout[0], multiplier_2_cout[1], multiplier_2_cout[2], multiplier_2_cout[3], multiplier_2_cout[4]);
endmodule

module x_selector (
  input  [4:0] y,
  input  [4:0] x,
  input  CLK
);

  wire [4:0] dmx0, dmx1, dmx2, dmx3, dmx4, dmx5, dmx6, dmx7, dmx8, dmx9, dmx10, dmx11, dmx12, dmx13, dmx14,
       dmx15, dmx16, dmx17, dmx18, dmx19, dmx20, dmx21, dmx22, dmx23, dmx24, dmx25, dmx26, dmx27, dmx28,
       dmx29, dmx30, dmx31;
  wire [31:0] decoder_1_out0;

  Decoder #(.select(5)) decoder_1 (
    .out0(decoder_1_out0[0]), .out1(decoder_1_out0[1]), .out2(decoder_1_out0[2]), .out3(decoder_1_out0[3]),
    .out4(decoder_1_out0[4]), .out5(decoder_1_out0[5]), .out6(decoder_1_out0[6]), .out7(decoder_1_out0[7]),
    .out8(decoder_1_out0[8]), .out9(decoder_1_out0[9]), .out10(decoder_1_out0[10]),
    .out11(decoder_1_out0[11]), .out12(decoder_1_out0[12]), .out13(decoder_1_out0[13]),
    .out14(decoder_1_out0[14]), .out15(decoder_1_out0[15]), .out16(decoder_1_out0[16]),
    .out17(decoder_1_out0[17]), .out18(decoder_1_out0[18]), .out19(decoder_1_out0[19]),
    .out20(decoder_1_out0[20]), .out21(decoder_1_out0[21]), .out22(decoder_1_out0[22]),
    .out23(decoder_1_out0[23]), .out24(decoder_1_out0[24]), .out25(decoder_1_out0[25]),
    .out26(decoder_1_out0[26]), .out27(decoder_1_out0[27]), .out28(decoder_1_out0[28]),
    .out29(decoder_1_out0[29]), .out30(decoder_1_out0[30]), .out31(decoder_1_out0[31]), .sel(dmx0));  // open: en
  Demultiplexer #(.select(5), .width(5)) demultiplexer_1 (
    .out0(dmx0), .out1(dmx1), .out2(dmx2), .out3(dmx3), .out4(dmx4), .out5(dmx5), .out6(dmx6), .out7(dmx7),
    .out8(dmx8), .out9(dmx9), .out10(dmx10), .out11(dmx11), .out12(dmx12), .out13(dmx13), .out14(dmx14),
    .out15(dmx15), .out16(dmx16), .out17(dmx17), .out18(dmx18), .out19(dmx19), .out20(dmx20), .out21(dmx21),
    .out22(dmx22), .out23(dmx23), .out24(dmx24), .out25(dmx25), .out26(dmx26), .out27(dmx27), .out28(dmx28),
    .out29(dmx29), .out30(dmx30), .out31(dmx31), .in(y), .sel(x));  // open: en
endmodule

module xy_selector (
  input  [4:0] x,
  input  [4:0] y,
  input  CLK,
  input  Reset,
  input  of,
  output [31:0] x0_output,
  output [31:0] x16_output,
  output [31:0] x1_output,
  output [31:0] x17_output,
  output [31:0] x2_output,
  output [31:0] x18_output,
  output [31:0] x3_output,
  output [31:0] x19_output,
  output [31:0] x4_output,
  output [31:0] x20_output,
  output [31:0] x5_output,
  output [31:0] x21_output,
  output [31:0] x6_output,
  output [31:0] x22_output,
  output [31:0] x7_output,
  output [31:0] x23_output,
  output [31:0] x8_output,
  output [31:0] x24_output,
  output [31:0] x9_output,
  output [31:0] x25_output,
  output [31:0] x10_output,
  output [31:0] x26_output,
  output [31:0] x11_output,
  output [31:0] x27_output,
  output [31:0] x12_output,
  output [31:0] x28_output,
  output [31:0] x13_output,
  output [31:0] x29_output,
  output [31:0] x14_output,
  output [31:0] x30_output,
  output [31:0] x15_output,
  output [31:0] x31_output
);

  wire and_2_out, and_3_out, and_4_out, and_5_out, and_6_out, and_7_out, and_8_out, and_9_out, and_10_out,
       and_11_out, and_12_out, and_13_out, and_14_out, and_15_out, and_16_out, and_17_out, and_18_out,
       and_19_out, and_20_out, and_21_out, and_22_out, and_23_out, and_24_out, and_25_out, and_26_out,
       and_27_out, and_28_out, and_29_out, and_30_out, and_31_out, and_32_out, and_33_out;
  wire [31:0] y_star, y_t;

  assign y_star = ~{32{of}} & y_t;  // AND_Gate and_1, 32 bits wide
  Decoder #(.select(5)) decoder_1 (
    .out0(y_t[0]), .out1(y_t[1]), .out2(y_t[2]), .out3(y_t[3]), .out4(y_t[4]), .out5(y_t[5]), .out6(y_t[6]),
    .out7(y_t[7]), .out8(y_t[8]), .out9(y_t[9]), .out10(y_t[10]), .out11(y_t[11]), .out12(y_t[12]),
    .out13(y_t[13]), .out14(y_t[14]), .out15(y_t[15]), .out16(y_t[16]), .out17(y_t[17]), .out18(y_t[18]),
    .out19(y_t[19]), .out20(y_t[20]), .out21(y_t[21]), .out22(y_t[22]), .out23(y_t[23]), .out24(y_t[24]),
    .out25(y_t[25]), .out26(y_t[26]), .out27(y_t[27]), .out28(y_t[28]), .out29(y_t[29]), .out30(y_t[30]),
    .out31(y_t[31]), .sel(y));  // open: en
  Register #(.width(32), .trigger("high")) x16 (.D(y_star), .Q(x16_output), .clk(and_2_out), .clr(Reset));  // open: en
  and and_2 (and_2_out, x[4], ~x[3], ~x[2], ~x[1], ~x[0], CLK);  // AND_Gate
  Register #(.width(32), .trigger("high")) x17 (.D(y_star), .Q(x17_output), .clk(and_3_out), .clr(Reset));  // open: en
  and and_3 (and_3_out, x[4], ~x[3], ~x[2], ~x[1], x[0], CLK);  // AND_Gate
  Register #(.width(32), .trigger("high")) x18 (.D(y_star), .Q(x18_output), .clk(and_4_out), .clr(Reset));  // open: en
  and and_4 (and_4_out, x[4], ~x[3], ~x[2], x[1], ~x[0], CLK);  // AND_Gate
  Register #(.width(32), .trigger("high")) x19 (.D(y_star), .Q(x19_output), .clk(and_5_out), .clr(Reset));  // open: en
  and and_5 (and_5_out, x[4], ~x[3], ~x[2], x[1], x[0], CLK);  // AND_Gate
  Register #(.width(32), .trigger("high")) x20 (.D(y_star), .Q(x20_output), .clk(and_6_out), .clr(Reset));  // open: en
  and and_6 (and_6_out, x[4], ~x[3], x[2], ~x[1], ~x[0], CLK);  // AND_Gate
  Register #(.width(32), .trigger("high")) x21 (.D(y_star), .Q(x21_output), .clk(and_7_out), .clr(Reset));  // open: en
  and and_7 (and_7_out, x[4], ~x[3], x[2], ~x[1], x[0], CLK);  // AND_Gate
  Register #(.width(32), .trigger("high")) x22 (.D(y_star), .Q(x22_output), .clk(and_8_out), .clr(Reset));  // open: en
  and and_8 (and_8_out, x[4], ~x[3], x[2], x[1], ~x[0], CLK);  // AND_Gate
  Register #(.width(32), .trigger("high")) x23 (.D(y_star), .Q(x23_output), .clk(and_9_out), .clr(Reset));  // open: en
  and and_9 (and_9_out, x[4], ~x[3], x[2], x[1], x[0], CLK);  // AND_Gate
  Register #(.width(32), .trigger("high")) x24 (.D(y_star), .Q(x24_output), .clk(and_10_out), .clr(Reset));  // open: en
  and and_10 (and_10_out, x[4], x[3], ~x[2], ~x[1], ~x[0], CLK);  // AND_Gate
  Register #(.width(32), .trigger("high")) x25 (.D(y_star), .Q(x25_output), .clk(and_11_out), .clr(Reset));  // open: en
  and and_11 (and_11_out, x[4], x[3], ~x[2], ~x[1], x[0], CLK);  // AND_Gate
  Register #(.width(32), .trigger("high")) x26 (.D(y_star), .Q(x26_output), .clk(and_12_out), .clr(Reset));  // open: en
  and and_12 (and_12_out, x[4], x[3], ~x[2], x[1], ~x[0], CLK);  // AND_Gate
  Register #(.width(32), .trigger("high")) x27 (.D(y_star), .Q(x27_output), .clk(and_13_out), .clr(Reset));  // open: en
  and and_13 (and_13_out, x[4], x[3], ~x[2], x[1], x[0], CLK);  // AND_Gate
  Register #(.width(32), .trigger("high")) x28 (.D(y_star), .Q(x28_output), .clk(and_14_out), .clr(Reset));  // open: en
  and and_14 (and_14_out, x[4], x[3], x[2], ~x[1], ~x[0], CLK);  // AND_Gate
  Register #(.width(32), .trigger("high")) x29 (.D(y_star), .Q(x29_output), .clk(and_15_out), .clr(Reset));  // open: en
  and and_15 (and_15_out, x[4], x[3], x[2], ~x[1], x[0], CLK);  // AND_Gate
  Register #(.width(32), .trigger("high")) x30 (.D(y_star), .Q(x30_output), .clk(and_16_out), .clr(Reset));  // open: en
  and and_16 (and_16_out, x[4], x[3], x[2], x[1], ~x[0], CLK);  // AND_Gate
  Register #(.width(32), .trigger("high")) x31 (.D(y_star), .Q(x31_output), .clk(and_17_out), .clr(Reset));  // open: en
  and and_17 (and_17_out, x[4], x[3], x[2], x[1], x[0], CLK);
  Register #(.width(32), .trigger("high")) x0 (.D(y_star), .Q(x0_output), .clk(and_18_out), .clr(Reset));  // open: en
  and and_18 (and_18_out, ~x[4], ~x[3], ~x[2], ~x[1], ~x[0], CLK);  // AND_Gate
  Register #(.width(32), .trigger("high")) x1 (.D(y_star), .Q(x1_output), .clk(and_19_out), .clr(Reset));  // open: en
  and and_19 (and_19_out, ~x[4], ~x[3], ~x[2], ~x[1], x[0], CLK);  // AND_Gate
  Register #(.width(32), .trigger("high")) x2 (.D(y_star), .Q(x2_output), .clk(and_20_out), .clr(Reset));  // open: en
  and and_20 (and_20_out, ~x[4], ~x[3], ~x[2], x[1], ~x[0], CLK);  // AND_Gate
  Register #(.width(32), .trigger("high")) x3 (.D(y_star), .Q(x3_output), .clk(and_21_out), .clr(Reset));  // open: en
  and and_21 (and_21_out, ~x[4], ~x[3], ~x[2], x[1], x[0], CLK);  // AND_Gate
  Register #(.width(32), .trigger("high")) x4 (.D(y_star), .Q(x4_output), .clk(and_22_out), .clr(Reset));  // open: en
  and and_22 (and_22_out, ~x[4], ~x[3], x[2], ~x[1], ~x[0], CLK);  // AND_Gate
  Register #(.width(32), .trigger("high")) x5 (.D(y_star), .Q(x5_output), .clk(and_23_out), .clr(Reset));  // open: en
  and and_23 (and_23_out, ~x[4], ~x[3], x[2], ~x[1], x[0], CLK);  // AND_Gate
  Register #(.width(32), .trigger("high")) x6 (.D(y_star), .Q(x6_output), .clk(and_24_out), .clr(Reset));  // open: en
  and and_24 (and_24_out, ~x[4], ~x[3], x[2], x[1], ~x[0], CLK);  // AND_Gate
  Register #(.width(32), .trigger("high")) x7 (.D(y_star), .Q(x7_output), .clk(and_25_out), .clr(Reset));  // open: en
  and and_25 (and_25_out, ~x[4], ~x[3], x[2], x[1], x[0], CLK);  // AND_Gate
  Register #(.width(32), .trigger("high")) x8 (.D(y_star), .Q(x8_output), .clk(and_26_out), .clr(Reset));  // open: en
  and and_26 (and_26_out, ~x[4], x[3], ~x[2], ~x[1], ~x[0], CLK);  // AND_Gate
  Register #(.width(32), .trigger("high")) x9 (.D(y_star), .Q(x9_output), .clk(and_27_out), .clr(Reset));  // open: en
  and and_27 (and_27_out, ~x[4], x[3], ~x[2], ~x[1], x[0], CLK);  // AND_Gate
  Register #(.width(32), .trigger("high")) x10 (.D(y_star), .Q(x10_output), .clk(and_28_out), .clr(Reset));  // open: en
  and and_28 (and_28_out, ~x[4], x[3], ~x[2], x[1], ~x[0], CLK);  // AND_Gate
  Register #(.width(32), .trigger("high")) x11 (.D(y_star), .Q(x11_output), .clk(and_29_out), .clr(Reset));  // open: en
  and and_29 (and_29_out, ~x[4], x[3], ~x[2], x[1], x[0], CLK);  // AND_Gate
  Register #(.width(32), .trigger("high")) x12 (.D(y_star), .Q(x12_output), .clk(and_30_out), .clr(Reset));  // open: en
  and and_30 (and_30_out, ~x[4], x[3], x[2], ~x[1], ~x[0], CLK);  // AND_Gate
  Register #(.width(32), .trigger("high")) x13 (.D(y_star), .Q(x13_output), .clk(and_31_out), .clr(Reset));  // open: en
  and and_31 (and_31_out, ~x[4], x[3], x[2], ~x[1], x[0], CLK);  // AND_Gate
  Register #(.width(32), .trigger("high")) x14 (.D(y_star), .Q(x14_output), .clk(and_32_out), .clr(Reset));  // open: en
  and and_32 (and_32_out, ~x[4], x[3], x[2], x[1], ~x[0], CLK);  // AND_Gate
  Register #(.width(32), .trigger("high")) x15 (.D(y_star), .Q(x15_output), .clk(and_33_out), .clr(Reset));  // open: en
  and and_33 (and_33_out, ~x[4], x[3], x[2], x[1], x[0], CLK);  // AND_Gate
endmodule
